# Fritzing sketch bike (saved by Fritzing 0.7.4b)
breadboards: 3

parts:
  Arduino1 = Arduino
  LED3 = LED - 5mm [color="Red (633nm)" package="5 mm [THT]"]
  LED6 = LED - 5mm [color="Red (633nm)" package="5 mm [THT]"]
  S3 = Reed switch [package=THT]
  LCD1 = LCD screen
  R1 = Resistor [tolerance=±5% resistance=220 package=THT]
  VCC1 = Battery
  S4 = Pushbutton [package="[THT]"]
  S5 = Pushbutton [package="[THT]"]
  R2 = Resistor [tolerance=±5% resistance=220 package=THT]
  R3 = Resistor [tolerance=±5% resistance=220 package=THT]
  R4 = Resistor [tolerance=±5% resistance=220 package=THT]
  R5 = Resistor [tolerance=±5% resistance=220 package=THT]
  R6 = Resistor [tolerance=±5% resistance=220 package=THT]
  S6 = Pushbutton [package="[THT]"]
  R7 = Resistor [tolerance=±5% resistance=220 package=THT]
  Part2 = Triple Axis Accelerometer Breakout - ADXL345
  R8 = Rotary Potentiometer (Small) [maximum_resistance=100kΩ]
  LED5 = LED - 5mm [color="Red (633nm)" package="5 mm [THT]"]
  Part3 = LED Matrix - Serial Interface - Red/Green/Blue  # not connected

nets:
  N1: Arduino1.D12, R6.Pin_1
  N2: Arduino1.D11, R5.Pin_1
  N3: Arduino1.D10, S5.Pin_1, S5.Pin_2, R3.Pin_0
  N4: Arduino1.D9, S4.Pin_1, S4.Pin_2, R2.Pin_0
  N5: Arduino1.D8, LCD1.RS
  N6: Arduino1.D7, S6.Pin_1, S6.Pin_2, R7.Pin_0
  N7: Arduino1.D6, LCD1.E
  N8: Arduino1.D5, LCD1.DB4
  N9: Arduino1.D4, LCD1.DB5
  N10: Arduino1.D3, LCD1.DB6
  N11: Arduino1.D2, LCD1.DB7
  3V3: Arduino1.3V3, Part2.VCC
  GND: Arduino1.GND, VCC1.-, Part2.GND
  N12: Arduino1.VIN, VCC1.+
  N13: Arduino1.A5, R1.Pin_0
  N14: LED3.cathode, LED6.cathode, LCD1.VSS, R2.Pin_1, R3.Pin_1, R8.leg2, LED5.cathode
  N15: LED3.anode, R4.Pin_0
  N16: LED6.anode, R6.Pin_0
  N17: S3.pin_2, S6.Pin_3, S6.Pin_4
  N18: LCD1.VDD, S4.Pin_3, S4.Pin_4, S5.Pin_3, S5.Pin_4, R8.leg1
  N19: LCD1.V0, R8.wiper
  N20: LCD1.R/W, R1.Pin_1, R7.Pin_1
  N21: R5.Pin_0, LED5.anode
